# Fritzing sketch rolling-door (saved by Fritzing 0.9.5d)
breadboards: 1

parts:
  R1 = Resistor [tolerance=±5% resistance=10k package=THT]
  D1 = Rectifier Diode [part_number=1N4001 package="300 mil [THT]"]
  Q1 = NPN-Transistor [package="TO92 [THT]"]

nets:
  N1: R1.Pin_0, Q1.C
  N2: D1.anode, Q1.B
